# Fritzing sketch robot_electronics (saved by Fritzing 0.9.3b)
perfboards: 1

parts:
  Raspberry_Pi_3 = Raspberry Pi 3 [part_number=RPI-3-V1.2]
  DC5 = DC_DC_XL4016 [package=board_screw]
  DC6 = DC_DC_XL4016 [package=board_screw]
  U3 = LIPO-2000mAh [package=lipo-2000]
  U4 = TCM8240MD [package=tcm8240md]
  S3 = Round Pushbutton
  L298N3 = L298N DC motor driver
  M5 = DC Motor
  M6 = DC Motor
  J19 = Screw terminal - 2 pins [package=THT]
  J20 = Screw terminal - 2 pins [package=THT]
  J21 = Screw terminal - 2 pins [package=THT]
  J22 = Screw terminal - 2 pins [package=THT]  # not connected
  J23 = Screw terminal - 2 pins [package=THT]  # not connected
  J24 = Screw terminal - 2 pins [package=THT]  # not connected
  J25 = Screw terminal - 2 pins [package=THT]  # not connected
  J26 = Screw terminal - 2 pins [package=THT]  # not connected
  J27 = Screw terminal - 2 pins [package=THT]
  J28 = Screw terminal - 2 pins [package=THT]  # not connected
  J29 = Screw terminal - 2 pins [package=THT]
  J30 = Screw terminal - 2 pins [package=THT]
  J31 = Screw terminal - 2 pins [package=THT]  # not connected
  J32 = Screw terminal - 2 pins [package=THT]
  U5 = ESP32-38PinWide [part_number=ESP32-38PinWide]
  Часть1 = LIDAR-Lite  # not connected
  LED1 = RGB LED (6 legs) [package="5 mm [THT]"]

nets:
  N1: Raspberry_Pi_3.GPIO3, Raspberry_Pi_3.5V, DC5.OUT-
  N2: Raspberry_Pi_3.GIPO4, Raspberry_Pi_3.GND, DC5.OUT+
  N3: DC5.IN+, J27.pin1
  N4: DC5.IN-, J27.pin2
  N5: DC6.IN+, J20.pin1
  N6: DC6.IN-, J20.pin2
  N7: U3.+, J21.pin1
  N8: U3.-, J19.pin2, J21.pin2
  N9: U4.DOUT0, U4.GND
  N10: S3.leg1, J29.pin1, J30.pin1
  N11: L298N3.OUT1, M5.pin_2
  N12: L298N3.OUT2, M5.pin_1
  N13: L298N3.OUT3, M6.pin_2
  N14: L298N3.OUT4, M6.pin_1
  N15: L298N3.IN1, U5.GPIO21
  N16: L298N3.IN2, U5.GPIO19
  N17: L298N3.IN3, U5.GPIO18
  N18: L298N3.IN4, U5.GPIO5
  N19: J32.pin1, U5.VIN, LED1.Green
  N20: U5.GPIO11, LED1.GND#1
  N21: U5.GPIO23, LED1.Blue1

notes:
  Left Motor 2
  Left Motor 1
  Camera
  ESP32
  L298n
  Raspberry Pi 5
  12 V to 5V
  12 V
  Emergency Button
  LIDAR
  RGB

custom parts:
  DC_DC_XL4016: DC-DC Converter step down voltage regulator XL4016 custom sketch.
  L298N DC motor driver: 2x DC motor driver with 78M05 positive voltage regulator (7..35 V) L298N: max 46 V, 2 A Set 5 V Enable jumper to enable 5 V regultor (needed for the L298N) and +5 V output at screw terminal or supply external +5 V at screw terminal Set ENA and/or ENB to +5 V to enable motor permanently or supply ENA and/or ENB with PWM signal IN1 and IN2 set rotation directory for motor A (OUT1/OUT2) IN2 and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
  ESP32-38PinWide: Generic 38-Pin ESP32 with wide format (only access to one side of pins on a breadboard) based on Stephen Lilley's HiLetgo ESP-WROOM-32 ESP32 ESP-32S Development Board.
  LIDAR-Lite: PulsedLight LIDAR-Lite Sensor
